# Fritzing sketch winderoo-with-oled (saved by Fritzing 0.9.10b)

parts:
  U1 = ESP32-38PinWide [part_number=ESP32-38PinWide]
  M1 = DC Motor [voltage_(max)=6V voltage_(min)=3V]
  L298N1 = L298N DC motor driver
  Part1 = OLED Monochrome 128x64 0.96 inch [part_number=326]

nets:
  N1: U1.GPIO25, L298N1.IN1
  N2: U1.GPIO26, L298N1.IN2
  VIN: U1.VIN, L298N1.12V, L298N1.5V#7, Part1.VIN
  N3: U1.GPIO21, Part1.MOSI_SDA
  N4: U1.GPIO22, Part1.SCLK_SCK
  GND: U1.GND, L298N1.GND, Part1.GND
  N5: M1.pin_1, L298N1.OUT2
  N6: M1.pin_2, L298N1.OUT1
  N7: L298N1.5V#9, L298N1.ENA
  N8: L298N1.5V#10, L298N1.ENB

custom parts:
  ESP32-38PinWide: Generic 38-Pin ESP32 with wide format (only access to one side of pins on a breadboard) based on Stephen Lilley's HiLetgo ESP-WROOM-32 ESP32 ESP-32S Development Board.
  L298N DC motor driver: 2x DC motor driver with 78M05 positive voltage regulator (7..35 V) L298N: max 46 V, 2 A Set 5 V Enable jumper to enable 5 V regultor (needed for the L298N) and +5 V output at screw terminal or supply external +5 V at screw terminal Set ENA and/or ENB to +5 V to enable motor permanently or supply ENA and/or ENB with PWM signal IN1 and IN2 set rotation directory for motor A (OUT1/OUT2) IN2 and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
  OLED Monochrome 128x64 0.96 inch: These displays are small, only about 1" diameter, but very readable due to the high contrast of an OLED display. This display is made of 128x64 individual white OLED pixels, each one is turned on or off by the controller chip. Because the display makes its own light, no backlight is required. This reduces the power required to run the OLED and is why the display has such high contrast; we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
